# Fritzing sketch bridge_v0.1 (saved by Fritzing 0.9.0b)
breadboards: 1

parts:
  part = Resistor [tolerance=±5% resistance=220 package=THT]  # not connected
  DS3231 = Real Time Clock Module - DS1307 RTC Breakout Board [part_number=DS3231]
  Part2 = Arduino Leonardo (Rev3b)
  DHT1 = DHT22 Humitidy and Temperature Sensor [part_number=DHT22]
  R1 = Resistor [tolerance=±5% resistance=4.7k package=THT]

nets:
  5V: DS3231.5V, Part2.5V, DHT1.VDD, R1.Pin_0
  GND: DS3231.GND, Part2.GND, DHT1.GND
  N1: DS3231.SCL, Part2.D3_PWM/SCL, Part2.SCL
  N2: DS3231.SDA, Part2.D2/SDA, Part2.SDA
  N3: Part2.D5_PWM, DHT1.DATA, R1.Pin_1

custom parts:
  DHT22 Humitidy and Temperature Sensor: DHT22 Humidity and Temperature Sensor
